# Fritzing sketch BlinkyDiodes (saved by Fritzing 0.9.3b)
breadboards: 1

parts:
  Raspberry_Pi_1 = Raspberry Pi 3 [part_number=RPI-3-V1.2]
  Q1 = NPN-Transistor [package="TO92 [THT]"]
  Q2 = NPN-Transistor [package="TO92 [THT]"]
  Q3 = NPN-Transistor [package="TO92 [THT]"]
  Q4 = NPN-Transistor [package="TO92 [THT]"]
  Q5 = NPN-Transistor [package="TO92 [THT]"]
  R1 = Resistor [tolerance=±5% resistance=220 package=THT]
  R2 = Resistor [tolerance=±5% resistance=220 package=THT]
  LED1 = LED - 5mm [color="Red (633nm)" package="5 mm [THT]"]
  LED2 = LED - 5mm [color="Red (633nm)" package="5 mm [THT]"]
  R3 = Resistor [tolerance=±5% resistance=220 package=THT]
  R4 = Resistor [tolerance=±5% resistance=220 package=THT]
  R5 = Resistor [tolerance=±5% resistance=220 package=THT]
  R6 = Resistor [tolerance=±5% resistance=220 package=THT]
  R7 = Resistor [tolerance=±5% resistance=220 package=THT]
  LED3 = LED - 5mm [color="Red (633nm)" package="5 mm [THT]"]
  LED4 = LED - 5mm [color="Red (633nm)" package="5 mm [THT]"]
  LED5 = LED - 5mm [color="Red (633nm)" package="5 mm [THT]"]
  LED6 = LED - 5mm [color="Red (633nm)" package="5 mm [THT]"]
  LED7 = LED - 5mm [color="Red (633nm)" package="5 mm [THT]"]
  LED8 = LED - 5mm [color="Red (633nm)" package="5 mm [THT]"]
  LED9 = LED - 5mm [color="Red (633nm)" package="5 mm [THT]"]
  LED10 = LED - 5mm [color="Red (633nm)" package="5 mm [THT]"]
  R8 = Resistor [tolerance=±5% resistance=220 package=THT]
  R9 = Resistor [tolerance=±5% resistance=220 package=THT]
  R10 = Resistor [tolerance=±5% resistance=220 package=THT]

nets:
  N1: Raspberry_Pi_1.GIPO5, R6.Pin_0
  N2: Raspberry_Pi_1.GIPO6, R5.Pin_0
  N3: Raspberry_Pi_1.GIPO13, R4.Pin_0
  N4: Raspberry_Pi_1.GIPO19, R3.Pin_0
  N5: Raspberry_Pi_1.GIPO26, R1.Pin_1
  N6: Raspberry_Pi_1.GND, Q1.E, Q2.E, Q3.E, Q4.E, Q5.E
  N7: Raspberry_Pi_1.5V, LED1.anode, LED4.anode, LED5.anode, LED6.anode, LED8.anode
  N8: Q1.B, R1.Pin_0
  N9: Q1.C, R2.Pin_0
  N10: Q2.B, R5.Pin_1
  N11: Q2.C, R9.Pin_0
  N12: Q3.B, R6.Pin_1
  N13: Q3.C, R10.Pin_1
  N14: Q4.B, R3.Pin_1
  N15: Q4.C, R7.Pin_0
  N16: Q5.B, R4.Pin_1
  N17: R2.Pin_1, LED2.cathode
  N18: LED1.cathode, LED2.anode
  N19: R7.Pin_1, LED9.cathode
  N20: LED3.cathode, R9.Pin_1
  N21: LED3.anode, LED6.cathode
  N22: LED4.cathode, LED7.anode
  N23: LED5.cathode, LED10.anode
  N24: LED7.cathode, R8.Pin_1
  N25: LED8.cathode, LED9.anode
  N26: LED10.cathode, R10.Pin_0
